// Logisim project Micros_Serie1Parcial2_KevinFlores.circ as structural Verilog: 10 circuits, main circuit RippleCarryAdder
module RippleCarryAdder (
  input  [3:0] A,
  input  [3:0] B,
  input  Cin,
  output [3:0] S,
  output Cout
);

  wire sum0_cout, sum1_cout, sum2_cout;

  Block_Adder_Ripple sum0 (.A(A[0]), .B(B[0]), .Cin(Cin), .S(S[0]), .Cout(sum0_cout));
  Block_Adder_Ripple sum1 (.A(A[1]), .B(B[1]), .Cin(sum0_cout), .S(S[1]), .Cout(sum1_cout));
  Block_Adder_Ripple sum2 (.A(A[2]), .B(B[2]), .Cin(sum1_cout), .S(S[2]), .Cout(sum2_cout));
  Block_Adder_Ripple sum3 (.A(A[3]), .B(B[3]), .Cin(sum2_cout), .S(S[3]), .Cout(Cout));
endmodule

module Block_Adder_Ripple (
  input  A,
  input  B,
  input  Cin,
  output S,
  output Cout
);

  wire and_1_out, and_2_out, xor_1_out;

  xor xor_1 (xor_1_out, A, B);
  xor xor_2 (S, xor_1_out, Cin);
  and and_1 (and_1_out, Cin, xor_1_out);
  and and_2 (and_2_out, A, B);
  or or_1 (Cout, and_1_out, and_2_out);
endmodule

module CarryLookaheadAdder (
  input  [3:0] A,
  input  [3:0] B,
  input  Cin,
  output [3:0] S,
  output Cout
);

  wire [3:0] Acarreo_Propagacion_c, Generador_P_G_g, Generador_P_G_p;

  Block_PgGenerator_Carry Generador_P_G (.A(A), .B(B), .P(Generador_P_G_p), .G(Generador_P_G_g));
  Block_Carry Acarreo_Propagacion (
    .P(Generador_P_G_p), .G(Generador_P_G_g), .C0(Cin), .C(Acarreo_Propagacion_c), .Cout(Cout));
  Block_Adder_Carry Sumador (.P(Generador_P_G_p), .C(Acarreo_Propagacion_c), .S(S));
endmodule

module Block_PgGenerator_Carry (
  input  [3:0] A,
  input  [3:0] B,
  output [3:0] P,
  output [3:0] G
);

  and and_1 (G[0], A[0], B[0]);
  and and_2 (G[1], A[1], B[1]);
  and and_3 (G[2], A[2], B[2]);
  and and_4 (G[3], A[3], B[3]);
  xor xor_1 (P[0], A[0], B[0]);
  xor xor_2 (P[1], A[1], B[1]);
  xor xor_3 (P[2], A[2], B[2]);
  xor xor_4 (P[3], A[3], B[3]);
endmodule

module Block_Carry (
  input  [3:0] P,
  input  [3:0] G,
  input  C0,
  output [3:0] C,
  output Cout
);

  wire and_1_out, and_2_out, and_3_out, and_4_out, and_5_out, and_6_out, and_7_out, and_8_out, and_9_out,
       and_10_out, and_11_out, and_12_out, and_13_out, and_14_out, and_15_out, and_16_out, and_17_out,
       and_18_out, and_19_out, and_20_out, or_1_out, or_2_out, or_3_out, or_4_out, or_5_out, or_6_out;

  and and_1 (and_1_out, C0, P[0]);
  and and_2 (and_2_out, C0, P[0]);
  and and_3 (and_3_out, G[0], P[1]);
  and and_4 (and_4_out, C0, P[0]);
  and and_5 (and_5_out, P[1], P[2]);
  and and_6 (and_6_out, G[0], P[1]);
  and and_7 (and_7_out, P[2], G[1]);
  and and_8 (and_8_out, C0, P[0]);
  and and_9 (and_9_out, P[1], P[2]);
  and and_10 (and_10_out, G[0], P[1]);
  and and_11 (and_11_out, P[2], P[3]);
  and and_12 (and_12_out, G[1], P[2]);
  and and_13 (and_13_out, P[3], G[2]);
  and and_14 (and_14_out, and_2_out, P[1]);
  and and_15 (and_15_out, and_4_out, and_5_out);
  and and_16 (and_16_out, and_6_out, P[2]);
  and and_17 (and_17_out, and_8_out, and_9_out);
  and and_18 (and_18_out, and_10_out, and_11_out);
  and and_19 (and_19_out, and_12_out, P[3]);
  and and_20 (and_20_out, and_17_out, P[3]);
  or or_1 (or_1_out, and_13_out, G[3]);
  or or_2 (or_2_out, and_14_out, and_3_out);
  or or_3 (or_3_out, and_15_out, and_16_out);
  or or_4 (or_4_out, and_7_out, G[2]);
  or or_5 (or_5_out, and_20_out, and_18_out);
  or or_6 (or_6_out, and_19_out, or_1_out);
  or or_7 (C[1], and_1_out, G[0]);
  or or_8 (C[2], or_2_out, G[1]);
  or or_9 (C[3], or_3_out, or_4_out);
  or or_10 (Cout, or_5_out, or_6_out);

  assign C[0] = C0;
endmodule

module Block_Adder_Carry (
  input  [3:0] P,
  input  [3:0] C,
  output [3:0] S
);

  xor xor_1 (S[0], P[0], C[0]);
  xor xor_2 (S[1], P[1], C[1]);
  xor xor_3 (S[2], P[2], C[2]);
  xor xor_4 (S[3], P[3], C[3]);
endmodule

module PrefixAdder (
  input  [3:0] A,
  input  [3:0] B,
  input  Cin,
  output [3:0] S,
  output Cout
);

  wire [3:0] block_parallel_prefix_1_gout, Generador_P_G_g, Generador_P_G_p;

  Block_PgGenerator_Prefix Generador_P_G (.A(A), .B(B), .P(Generador_P_G_p), .G(Generador_P_G_g));
  Block_Parallel_Prefix block_parallel_prefix_1 (
    .P(Generador_P_G_p), .G(Generador_P_G_g), .Cin(Cin), .Gout(block_parallel_prefix_1_gout), .Cout(Cout));
  Block_Adder_Prefix block_adder_prefix_1 (.A(A), .B(B), .G2in(block_parallel_prefix_1_gout), .S(S));
endmodule

module Block_PgGenerator_Prefix (
  input  [3:0] A,
  input  [3:0] B,
  output [3:0] P,
  output [3:0] G
);

  and and_1 (G[0], A[0], B[0]);
  or or_1 (P[0], A[0], B[0]);
  and and_2 (G[1], A[1], B[1]);
  or or_2 (P[1], A[1], B[1]);
  and and_3 (G[2], A[2], B[2]);
  or or_3 (P[2], A[2], B[2]);
  and and_4 (G[3], A[3], B[3]);
  or or_4 (P[3], A[3], B[3]);
endmodule

module Block_Parallel_Prefix (
  input  [3:0] P,
  input  [3:0] G,
  input  Cin,
  output [3:0] Gout,
  output Cout
);

  wire and_1_out, and_2_out, and_3_out, and_4_out, and_5_out, and_6_out, or_1_out;

  and and_1 (and_1_out, Cin, P[0]);
  and and_2 (and_2_out, G[1], P[2]);
  and and_3 (and_3_out, P[1], P[2]);
  or or_1 (or_1_out, and_2_out, G[2]);
  or or_2 (Gout[1], and_1_out, G[0]);
  and and_4 (and_4_out, Gout[1], P[1]);
  and and_5 (and_5_out, Gout[1], and_3_out);
  or or_3 (Gout[2], and_4_out, G[1]);
  or or_4 (Gout[3], and_5_out, or_1_out);
  and and_6 (and_6_out, Gout[3], P[3]);
  or or_5 (Cout, and_6_out, G[3]);

  assign Gout[0] = Cin;
endmodule

module Block_Adder_Prefix (
  input  [3:0] A,
  input  [3:0] B,
  input  [3:0] G2in,
  output [3:0] S
);

  wire xor_1_out, xor_2_out, xor_3_out, xor_4_out;

  xor xor_1 (xor_1_out, A[0], B[0]);
  xor xor_2 (xor_2_out, A[1], B[1]);
  xor xor_3 (xor_3_out, A[2], B[2]);
  xor xor_4 (xor_4_out, A[3], B[3]);
  xor xor_5 (S[0], xor_1_out, G2in[0]);
  xor xor_6 (S[1], xor_2_out, G2in[1]);
  xor xor_7 (S[2], xor_3_out, G2in[2]);
  xor xor_8 (S[3], xor_4_out, G2in[3]);
endmodule
